# Fritzing sketch OLED Hookup (saved by Fritzing 0.9.3b)

parts:
  U1 = NodeMCU V1.0
  Squix1 = OLED 0.96" 128x64 I2C SSD1306

nets:
  N1: U1.RX, Squix1.SCA
  N2: U1.TX, Squix1.SCL
  GND: U1.GND, Squix1.GND
  3V3: U1.3V3, Squix1.VCC

custom parts:
  NodeMCU V1.0: ESP8266 based NodeMCU
